// Logisim project equality.1052751.circ as structural Verilog: 3 circuits, main circuit equality
module main (
  input  in_1,
  input  in_2,
  output out_3
);

  wire and_1_out, and_2_out, not_1_out, not_2_out, or_1_out;

  not not_1 (not_1_out, in_1);
  not not_2 (not_2_out, in_2);
  and and_1 (and_1_out, not_1_out, in_2);
  and and_2 (and_2_out, in_1, not_2_out);
  or or_1 (or_1_out, and_1_out, and_2_out);
  not not_3 (out_3, or_1_out);

  // Notes on the sheet:
  //   x XOR y
endmodule

module equality (
  input  [2:0] in_1,
  input  [2:0] in_2,
  output out_3
);

  wire main_1_out_3, main_2_out_3, main_3_out_3;

  main main_1 (.in_1(in_1[0]), .in_2(in_2[0]), .out_3(main_1_out_3));
  main main_2 (.in_1(in_1[1]), .in_2(in_2[1]), .out_3(main_2_out_3));
  main main_3 (.in_1(in_1[2]), .in_2(in_2[2]), .out_3(main_3_out_3));
  and and_1 (out_3, main_1_out_3, main_2_out_3, main_3_out_3);
endmodule

module _8_Bit_Not (
  input  [7:0] in_1,
  output [7:0] out_2
);

  not not_1 (out_2[6], in_1[6]);
  not not_2 (out_2[7], in_1[7]);
  not not_3 (out_2[0], in_1[0]);
  not not_4 (out_2[1], in_1[1]);
  not not_5 (out_2[2], in_1[2]);
  not not_6 (out_2[3], in_1[3]);
  not not_7 (out_2[4], in_1[4]);
  not not_8 (out_2[5], in_1[5]);
endmodule
